# Fritzing sketch motor_i2c_module (saved by Fritzing 1.0.8)
circuit board: 7.0cm x 9.0cm

parts:
  U1_Blue_Pill = STM32F103C8T6 Blue Pill
  U2_ZK-5AD_№1 = motor driver ZK-5AD
  U3_ZK-5AD_№2 = motor driver ZK-5AD
  J7_ZK-5AD_№1 = male pin header, 7 pins [form="♂ (male)"]
  J8_ZK-5AD_№2 = male pin header, 7 pins [form="♂ (male)"]
  M1 = JGB37-520 Gear Motor with Hall Encoder
  M2 = JGB37-520 Gear Motor with Hall Encoder
  M3 = JGB37-520 Gear Motor with Hall Encoder
  M4 = JGB37-520 Gear Motor with Hall Encoder
  J3_M1 = male pin header, 6 pins [form="♂ (male)"]
  J4_M2 = male pin header, 6 pins [form="♂ (male)"]
  J5_M3 = male pin header, 6 pins [form="♂ (male)"]
  J6_M4 = male pin header, 6 pins [form="♂ (male)"]
  J1_I2C = male pin header, 4 pins [form="♂ (male)"]
  D1 = Schottky Diode [package="300 mil [THT]"]
  R1 = Resistor [resistance=4.7kΩ tolerance=±5% power=0.25W package=THT]
  R2 = Resistor [resistance=4.7kΩ tolerance=±5% power=0.25W package=THT]
  R3 = Resistor [resistance=10kΩ tolerance=±5% power=0.25W package=THT]
  R4 = Resistor [resistance=10kΩ tolerance=±5% power=0.25W package=THT]
  R5 = Resistor [resistance=10kΩ tolerance=±5% power=0.25W package=THT]
  R6 = Resistor [resistance=10kΩ tolerance=±5% power=0.25W package=THT]
  R7 = Resistor [resistance=10kΩ tolerance=±5% power=0.25W package=THT]
  R8 = Resistor [resistance=10kΩ tolerance=±5% power=0.25W package=THT]
  R9 = Resistor [resistance=10kΩ tolerance=±5% power=0.25W package=THT]
  R10 = Resistor [resistance=10kΩ tolerance=±5% power=0.25W package=THT]

nets:
  GND: U1_Blue_Pill.GND, U2_ZK-5AD_№1.Pin_1, U2_ZK-5AD_№1.Pin_12, U3_ZK-5AD_№2.Pin_1, U3_ZK-5AD_№2.Pin_12, J7_ZK-5AD_№1.pin1, J8_ZK-5AD_№2.pin1, M1.GND, M2.GND, M3.GND, M4.GND, J3_M1.pin2, J4_M2.pin2, J5_M3.pin2, J6_M4.pin2, J1_I2C.pin1, R3.Pin_0, R4.Pin_0, R5.Pin_0, R6.Pin_0, R7.Pin_0, R8.Pin_0, R9.Pin_0, R10.Pin_0
  +3V3: U1_Blue_Pill.3.3V, M1.VCC, M2.VCC, M3.VCC, M4.VCC, J3_M1.pin5, J4_M2.pin5, J5_M3.pin5, J6_M4.pin5, R1.Pin_0, R2.Pin_0
  SDA: U1_Blue_Pill.PB11, J1_I2C.pin4, R2.Pin_1
  SCL: U1_Blue_Pill.PB10, J1_I2C.pin3, R1.Pin_1
  M4_IN2: U1_Blue_Pill.PB1, U3_ZK-5AD_№2.Pin_6, J8_ZK-5AD_№2.pin6, R10.Pin_1
  M4_IN1: U1_Blue_Pill.PB0, U3_ZK-5AD_№2.Pin_5, J8_ZK-5AD_№2.pin5, R9.Pin_1
  M3_IN2: U1_Blue_Pill.PA7, U3_ZK-5AD_№2.Pin_4, J8_ZK-5AD_№2.pin4, R8.Pin_1
  M3_IN1: U1_Blue_Pill.PA6, U3_ZK-5AD_№2.Pin_3, J8_ZK-5AD_№2.pin3, R7.Pin_1
  M2_IN2: U1_Blue_Pill.PA3, U2_ZK-5AD_№1.Pin_6, J7_ZK-5AD_№1.pin6, R6.Pin_1
  M2_IN1: U1_Blue_Pill.PA2, U2_ZK-5AD_№1.Pin_5, J7_ZK-5AD_№1.pin5, R5.Pin_1
  M1_IN2: U1_Blue_Pill.PA1, U2_ZK-5AD_№1.Pin_4, J7_ZK-5AD_№1.pin4, R4.Pin_1
  M1_IN1: U1_Blue_Pill.PA0, U2_ZK-5AD_№1.Pin_3, J7_ZK-5AD_№1.pin3, R3.Pin_1
  M3_ENC_A: U1_Blue_Pill.PB12, M3.C1, J5_M3.pin3
  M3_ENC_B: U1_Blue_Pill.PB13, M3.C2, J5_M3.pin4
  M4_ENC_A: U1_Blue_Pill.PB14, M4.C1, J6_M4.pin3
  M4_ENC_B: U1_Blue_Pill.PB15, M4.C2, J6_M4.pin4
  M1_ENC_A: U1_Blue_Pill.PA8, M1.C1, J3_M1.pin3
  M1_ENC_B: U1_Blue_Pill.PA9, M1.C2, J3_M1.pin4
  M2_ENC_A: U1_Blue_Pill.PB6, M2.C1, J4_M2.pin3
  M2_ENC_B: U1_Blue_Pill.PB7, M2.C2, J4_M2.pin4
  +5V: U1_Blue_Pill.5V, D1.cathode
  ZK1_3V3: U2_ZK-5AD_№1.Pin_2, J7_ZK-5AD_№1.pin2
  ZK1_VT: U2_ZK-5AD_№1.Pin_7, J7_ZK-5AD_№1.pin7
  M2_OUT2: U2_ZK-5AD_№1.Pin_8, M2.M2, J4_M2.pin6
  M2_OUT1: U2_ZK-5AD_№1.Pin_9, M2.M1, J4_M2.pin1
  M1_OUT2: U2_ZK-5AD_№1.Pin_10, M1.M2, J3_M1.pin6
  M1_OUT1: U2_ZK-5AD_№1.Pin_11, M1.M1, J3_M1.pin1
  +12V: U2_ZK-5AD_№1.Pin_13, U3_ZK-5AD_№2.Pin_13
  ZK2_3V3: U3_ZK-5AD_№2.Pin_2, J8_ZK-5AD_№2.pin2
  ZK2_VT: U3_ZK-5AD_№2.Pin_7, J8_ZK-5AD_№2.pin7
  M4_OUT2: U3_ZK-5AD_№2.Pin_8, M4.M2, J6_M4.pin6
  M4_OUT1: U3_ZK-5AD_№2.Pin_9, M4.M1, J6_M4.pin1
  M3_OUT2: U3_ZK-5AD_№2.Pin_10, M3.M2, J5_M3.pin6
  M3_OUT1: U3_ZK-5AD_№2.Pin_11, M3.M1, J5_M3.pin1
  +5V_EXT: J1_I2C.pin2, D1.anode

notes:
  Подключение: doc/motor_i2c_module/wiring.md
  U2 ZK-5AD №1 — моторы M1, M2
  U3 ZK-5AD №2 — моторы M3, M4
  R3–R10 10 кОм — входы ZK-5AD к GND
  R1, R2 4.7 кОм — SCL, SDA к 3.3 В
  J1: GND, 5V, SCL, SDA; D1 — диод Шоттки
  в линии 5 В от master к 5V Blue Pill
  ZK-5AD — вне платы, кабелем Dupont
  7 проводов к J7 (№1) и J8 (№2)
  Перемычка M-GND — GND под ZK-5AD:
  общая земля модуля (в компоненте
  Fritzing эти выводы не соединены)
  12 В — от источника на клеммники ZK-5AD
  J7 ZK1
  GND
  3V3
  IN1
  IN2
  IN3
  IN4
  VT
  J8 ZK2
  J4 M2
  M+
  A
  B
  M-
  J3 M1
  J6 M4
  J5 M3
  5V
  SCL
  SDA
  J1 I2C

custom parts:
  STM32F103C8T6 Blue Pill: STM32F103C8T6 "Blue Pill" board, top view with micro USB on the left. Header 1 (top row, left to right): G G 3.3 R B11 B10 B1 B0 A7 A6 A5 A4 A3 A2 A1 A0 C15 C14 C13 VB. Header 2 (bottom row, left to right): B12 B13 B14 B15 A8 A9 A10 A11 A12 A15 B3 B4 B5 B6 B7 B8 B9 5V G 3.3. SWD header at the right end (top to bottom): GND, SWCLK, SWDIO, 3.3V. BOOT0/BOOT1 jumpers (0 = GND, 1 = 3.3V). All GND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
  motor driver ZK-5AD: 5A Dual Motor Drive Module Reverse PWM Speed Regulation Double H Bridge L298N Module DC 3.0V-14V.
  JGB37-520 Gear Motor with Hall Encoder: JGB37-520 DC gear motor (37 mm gearbox, 6 mm D-shaft) with magnetic Hall encoder. 6-pin PH2.0 cable: 1 M1 motor+ (red), 2 GND (black), 3 C1 encoder A (yellow), 4 C2 encoder B (green), 5 VCC 3.3-5V (blue), 6 M2 motor- (white). Encoder gives 11 pulses per motor revolution per channel; counts per output-shaft revolution = 11 x gear ratio (x4 with quadrature decoding). M1/M2 must be driven through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
